// Logisim project method1.circ as structural Verilog: 1 circuit, main circuit main
module main (
  input  in_1,
  input  in_2,
  input  in_3,
  input  in_4,
  output out_5
);

  wire a_rst, and_1_out, and_2_out, and_3_out, and_4_out, and_5_out, and_6_out, clock_1_out, clock_2_out,
       clock_3_out, clock_4_out, d_ff_1_q, d_ff_1_qn, d_ff_2_qn, d_ff_3_q, d_ff_3_qn, d_ff_4_qn, d_ff_5_q,
       d_ff_5_qn, d_ff_6_q, d_ff_6_qn, hr_clk, multiplexer_1_out, multiplexer_2_out, nor_1_out, nor_2_out,
       nor_4_out, nor_5_out, tens_0, xor_3_out, xor_4_out, xor_5_out, xor_6_out, xor_7_out, xor_8_out,
       xor_9_out, zero_det;
  wire [3:0] counter_4_q, counter_5_q, counter_7_q, counter_8_q, counter_9_q, counter_10_q, counter_11_q,
       counter_12_q, multiplexer_6_out, multiplexer_10_out, ones;
  wire [3:1] counter_1_q, counter_2_q;

  // NoConnect on counter_1_q[3]
  // NoConnect on counter_1_q[2]
  // NoConnect on counter_1_q[1]
  Counter #(.max('h9), .trigger("falling"), .width(4)) counter_1 (
    .load(1'b0), .count(1'b1), .Q({counter_1_q, tens_0}), .up(1'b1), .clk(ones[3]), .clr(and_1_out));  // open: D, carry
  Clock clock_1 (.out(clock_1_out));
  // NoConnect on counter_2_q[3]
  // NoConnect on counter_2_q[2]
  // NoConnect on counter_2_q[1]
  Counter #(.max('h9), .trigger("falling"), .width(4)) counter_2 (
    .load(1'b0), .count(1'b1), .Q({counter_2_q, tens_0}), .up(1'b1), .clk(ones[3]), .clr(and_4_out));  // open: D, carry
  nor nor_1 (nor_1_out, tens_0, ones[0], ones[1]);
  xor xor_1 (hr_clk, and_2_out, in_2);
  // XOR_Gate xor_2 has open pins: in0=and_3_out, in1=in_4, out=open
  Clock clock_2 (.out(clock_2_out));
  D_Flip_Flop d_ff_1 (.D(d_ff_1_qn), .clk(clock_1_out), .Q(d_ff_1_q), .Qn(d_ff_1_qn));  // open: preset, reset
  Counter #(.max('h9), .trigger("falling"), .width(4)) counter_3 (
    .load(1'b0), .count(1'b1), .Q(ones), .up(1'b1), .clk(hr_clk), .clr(and_1_out));  // open: D, carry
  nor nor_2 (nor_2_out, nor_1_out, nor_1_out, nor_1_out);
  nor nor_3 (zero_det, nor_2_out, ones[2], ones[3]);
  Counter #(.max('h9), .trigger("falling"), .width(4)) counter_4 (
    .load(1'b0), .count(1'b1), .Q(counter_4_q), .up(1'b1), .clk(counter_7_q[3]), .clr(and_2_out));  // open: D, carry
  Counter #(.max('h9), .trigger("falling"), .width(4)) counter_5 (
    .load(1'b0), .count(1'b1), .Q(counter_5_q), .up(1'b1), .clk(counter_8_q[3]), .clr(and_3_out));  // open: D, carry
  D_Flip_Flop d_ff_2 (.D(d_ff_2_qn), .clk(clock_2_out), .Qn(d_ff_2_qn));  // open: Q, preset, reset
  D_Flip_Flop d_ff_3 (.D(d_ff_3_qn), .clk(d_ff_1_qn), .Q(d_ff_3_q), .Qn(d_ff_3_qn));  // open: preset, reset
  Counter #(.max('h9), .trigger("falling"), .width(4)) counter_6 (
    .load(1'b0), .count(1'b1), .Q(ones), .up(1'b1), .clk(hr_clk), .clr(and_4_out));  // open: D, carry
  nor nor_4 (nor_4_out, tens_0, ones[0], ones[1]);
  nor nor_5 (nor_5_out, nor_4_out, nor_4_out, nor_4_out);
  and and_1 (and_1_out, tens_0, ones[1]);
  // Probe on zero_det
  and and_2 (and_2_out, counter_4_q[2], counter_4_q[1]);
  and and_3 (and_3_out, counter_5_q[2], counter_5_q[1]);
  D_Flip_Flop d_ff_4 (.D(d_ff_4_qn), .clk(d_ff_2_qn), .Qn(d_ff_4_qn));  // open: Q, preset, reset
  D_Flip_Flop d_ff_5 (.D(d_ff_5_qn), .clk(d_ff_3_qn), .Q(d_ff_5_q), .Qn(d_ff_5_qn));  // open: preset, reset
  and and_4 (and_4_out, tens_0, ones[1]);
  // Probe on zero_det
  nor nor_6 (zero_det, nor_5_out, ones[2], ones[3]);
  D_Flip_Flop d_ff_6 (.D(d_ff_6_qn), .clk(a_rst), .Q(d_ff_6_q), .Qn(d_ff_6_qn));  // open: preset, reset
  Counter #(.max('h9), .trigger("falling"), .width(4)) counter_7 (
    .load(1'b0), .count(1'b1), .Q(counter_7_q), .up(1'b1), .clk(xor_3_out), .clr(1'b0));  // open: D, carry
  xor xor_3 (xor_3_out, and_5_out, in_1);
  Counter #(.max('h9), .trigger("falling"), .width(4)) counter_8 (
    .load(1'b0), .count(1'b1), .Q(counter_8_q), .up(1'b1), .clk(xor_4_out), .clr(1'b0));  // open: D, carry
  xor xor_4 (xor_4_out, and_6_out, in_3);
  D_Flip_Flop d_ff_7 (.D(out_5), .clk(d_ff_4_qn), .Qn(out_5));  // open: Q, preset, reset
  // Probe on multiplexer_1_out
  Multiplexer #(.enable("false")) multiplexer_1 (.in0(tens_0), .in1(1'b1), .out(multiplexer_1_out), .sel(zero_det));
  // Probe on multiplexer_2_out
  Multiplexer #(.enable("false")) multiplexer_2 (.in0(tens_0), .in1(1'b1), .out(multiplexer_2_out), .sel(zero_det));
  // Probe on d_ff_6_q
  // Probe on d_ff_6_qn
  Counter #(.max('h9), .trigger("falling"), .width(4)) counter_9 (
    .load(1'b0), .count(1'b1), .Q(counter_9_q), .up(1'b1), .clk(counter_10_q[3]), .clr(xor_6_out));  // open: D, carry
  xor xor_5 (xor_5_out, and_5_out, in_1);
  and and_5 (and_5_out, counter_9_q[2], counter_9_q[1]);
  Clock clock_3 (.out(clock_3_out));
  xor xor_6 (xor_6_out, xor_5_out, in_2);
  xor xor_7 (xor_7_out, and_6_out, in_3);
  xor xor_8 (xor_8_out, xor_7_out, in_4);
  Multiplexer #(.enable("false")) multiplexer_3 (.in0(ones[3]), .in1(1'b0), .out(multiplexer_6_out[3]), .sel(zero_det));
  Multiplexer #(.enable("false")) multiplexer_4 (.in0(ones[2]), .in1(1'b0), .out(multiplexer_6_out[2]), .sel(zero_det));
  Multiplexer #(.enable("false")) multiplexer_5 (.in0(ones[1]), .in1(1'b1), .out(multiplexer_6_out[1]), .sel(zero_det));
  Multiplexer #(.enable("false")) multiplexer_6 (.in0(ones[0]), .in1(1'b0), .out(multiplexer_6_out[0]), .sel(zero_det));
  Multiplexer #(.enable("false")) multiplexer_7 (
    .in0(ones[3]), .in1(1'b0), .out(multiplexer_10_out[3]), .sel(zero_det));
  Multiplexer #(.enable("false")) multiplexer_8 (
    .in0(ones[2]), .in1(1'b0), .out(multiplexer_10_out[2]), .sel(zero_det));
  Multiplexer #(.enable("false")) multiplexer_9 (
    .in0(ones[1]), .in1(1'b1), .out(multiplexer_10_out[1]), .sel(zero_det));
  Multiplexer #(.enable("false")) multiplexer_10 (
    .in0(ones[0]), .in1(1'b0), .out(multiplexer_10_out[0]), .sel(zero_det));
  Counter #(.max('h9), .trigger("falling"), .width(4)) counter_10 (
    .load(1'b0), .count(1'b1), .Q(counter_10_q), .up(1'b1), .clk(clock_3_out), .clr(xor_6_out));  // open: D, carry
  Counter #(.max('h9), .trigger("falling"), .width(4)) counter_11 (
    .load(1'b0), .count(1'b1), .Q(counter_11_q), .up(1'b1), .clk(counter_12_q[3]), .clr(xor_8_out));  // open: D, carry
  and and_6 (and_6_out, counter_11_q[2], counter_11_q[1]);
  Clock clock_4 (.out(clock_4_out));
  xor xor_9 (xor_9_out, in_3, in_4);
  // Probe on multiplexer_6_out
  // Probe on multiplexer_10_out
  Counter #(.max('h9), .trigger("falling"), .width(4)) counter_12 (
    .load(1'b0), .count(1'b1), .Q(counter_12_q), .up(1'b1), .clk(clock_4_out), .clr(xor_9_out));  // open: D, carry

  // Notes on the sheet:
  //   Hours_1
  //   min button ->
  //   hour button ->
  //   f
  //   hour_1
  //   Hours_0
  //   00 Detector
  //   2
  //   3
  //   1
  //   f/2
  //   hour_0
  //   2
  //   4
  //   1
  //   min_1
  //   min_1
  //   f/4
  //   00 Detector
  //   3
  //   min_0
  //   1
  //   4
  //   1
  //   Method 1: Zero Detection
  //   AM/PM
  //   2
  //   min_0
  //   f/8
  //   sec_1
  //   2
  //   4
  //   Output
  //   Output
  //   sec_0
  //   3
  //   sec_1
  //   sec_0
endmodule
