// Logisim project method2.circ as structural Verilog: 1 circuit, main circuit main
module main (
);

  wire a_rst_ones, a_rst_tens, adder_1_cout, and_1_out, and_2_out, clock_1_out, d_ff_1_q, d_ff_1_qn;
  wire [0:0] not_1_out;
  wire [3:0] ones, ones_output, tens;

  Counter #(.max('h9), .trigger("falling"), .width(4)) counter_1 (
    .load(1'b0), .count(1'b1), .Q(tens), .up(1'b1), .clk(ones[3]), .clr(a_rst_tens));  // open: D, carry
  D_Flip_Flop d_ff_1 (.D(d_ff_1_qn), .clk(a_rst_tens), .Q(d_ff_1_q), .Qn(d_ff_1_qn));  // open: preset, reset
  // Probe on d_ff_1_q
  // Probe on d_ff_1_qn
  Counter #(.max('h9), .trigger("falling"), .width(4)) counter_2 (
    .load(1'b0), .count(1'b1), .Q(ones), .up(1'b1), .clk(clock_1_out), .clr(a_rst_ones));  // open: D, carry
  Clock clock_1 (.out(clock_1_out));
  // Probe on tens
  // Probe on ones_output
  not not_1 (not_1_out[0], tens[0]);
  Adder #(.width(4)) adder_1 (
    .a({tens[3:1], not_1_out[0]}), .b(ones), .out(ones_output), .cin(1'b0), .cout(adder_1_cout));
  // NoConnect on adder_1_cout
  and and_1 (and_1_out, ones[1], ones[0]);
  and and_2 (and_2_out, ones[3], ones[0]);
  Multiplexer #(.enable("false")) multiplexer_1 (.in0(1'b0), .in1(and_1_out), .out(a_rst_tens), .sel(tens[0]));
  Multiplexer #(.enable("false")) multiplexer_2 (.in0(and_2_out), .in1(and_1_out), .out(a_rst_ones), .sel(tens[0]));

  // Other names for the same wires on the sheet: tens_Qo = tens[0]

  // Notes on the sheet:
  //   Hours_1
  //   AM/PM
  //   Hours_0
  //   Output
  //   Method 2: Adder 
  //   Adder Logic
endmodule
